# Fritzing sketch WaterDropper (saved by Fritzing 0.9.3b)
circuit board: 8.46667cm x 5.64444cm
breadboards: 1

parts:
  Q2 = NPN-Transistor [package="TO92 [THT]"]
  Q3 = NPN-Transistor [package="TO92 [THT]"]
  R3 = Resistor [tolerance=±1% resistance=10k package=THT]
  R2 = Resistor [tolerance=±1% resistance=10k package=THT]
  R1 = Resistor [tolerance=±1% resistance=10k package=THT]
  Part1 = Arduino Uno (Rev3)
  J1 = Power Jack [package=power_jack_slot]
  J2 = Power Jack [package=power_jack_slot]
  Q4 = Basic FET N-Channel [package="TO220 [THT]"]
  U1 = 3.5mm Audio Jack [package=audio-jack-3.5mm-smd]
  S1 = Pushbutton [package="[THT]"]
  R4 = Resistor [tolerance=±5% resistance=220 package=THT]

nets:
  GND: Q2.E, Q3.E, R3.Pin_1, R2.Pin_1, R1.Pin_1, Part1.GND, J1.GNDBREAK, J1.GND, Q4.source, U1.SLEEVE, R4.Pin_1
  N1: Q2.B, R2.Pin_0, Part1.D9_PWM
  N2: Q2.C, U1.LEFT
  N3: Q3.B, R3.Pin_0, Part1.D8
  N4: Q3.C, U1.RIGHT
  N5: R1.Pin_0, Part1.D10_PWM/SS, Q4.gate
  N6: Part1.D2, S1.Pin_1, S1.Pin_2, R4.Pin_0
  N7: Part1.5V, S1.Pin_3, S1.Pin_4
  N8: J1.PWR, J2.PWR
  N9: J2.GNDBREAK, J2.GND, Q4.drain

notes:
  Top (left): shutter
  Ring (right): metering
  Sleeve: ground
  Solenoid valve
  12 V DC source
